# Fritzing sketch Desafio_esquema (saved by Fritzing 0.9.3b)

parts:
  S1 = Pushbutton [package=THT]
  Led = LED - 5mm [color="Red (660nm)" package="5 mm [THT]"]
  R1 = Resistor [tolerance=±5% resistance=10k package=THT]
  R2 = Resistor [tolerance=±5% resistance=1k package=THT]
  Raspberry_Pi_Zero1 = Raspberry Pi Zero

nets:
  3.3V: S1.leg0
  N1: S1.leg1, R1.Pin_0, Raspberry_Pi_Zero1.GPIO17
  N2: Led.cathode, R2.Pin_0
  N3: Led.anode, Raspberry_Pi_Zero1.GPIO26
  GND: R1.Pin_1, R2.Pin_1
